# Fritzing sketch motorDC-driver (saved by Fritzing 1.0.1rc)
breadboards: 1

parts:
  DC_Motor = DC Power Supply [part_number="6 V" package="DC Power"]
  Q1 = NPN-Transistor [part_number=2n2222a package="SOT-23 [SMD]"]
  R2 = Resistor [tolerance=±5% resistance=1k package="0805 [SMD]"]
  M1 = DC Motor [voltage_(max)=6V voltage_(min)=3V]
  M2 = DOIT Esp32 DevKit v1 (30 pins long, 11 pins width) [part_number=ESP32S-PIN30]

nets:
  N1: DC_Motor.V+, M1.pin_2
  N2: DC_Motor.V-, Q1.2, M2.GND
  N3: Q1.0, R2.Pin_1
  N4: Q1.1, M1.pin_1
  N5: R2.Pin_0, M2.D19

notes:
  6V
  2N2222A
  Motor DC
  300 mA

custom parts:
  DOIT Esp32 DevKit v1 (30 pins long, 11 pins width): The DOIT Esp32 DevKit v1 is one of the development board created by DOIT to evaluate the ESP-WROOM-32 module. It is based on the ESP32 microcontroller that boasts Wifi, Bluetooth, Ethernet and Low Power support all in a single chip. (vanepp) made breadboard work, adjusted pin numbering and labels and reduced size of schematic and cleaned up pcb. This chip is 30pins long (2 x15) and 11 pins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
