# Fritzing sketch montaje-led-medir-corriente (saved by Fritzing 0.9.6b)
breadboards: 1

parts:
  R1 = Resistor [tolerance=±5% power=0.25 resistance=10k package=THT]
  LED1 = smd LED [color="Red (633nm)" package="0805 [SMD]"]
  DC_Power1 = DC Power Supply [package="DC Power"]
  VM1 = Multimeter (DC Current)

nets:
  N1: R1.Pin_0, VM1.COM_Probe
  N2: R1.Pin_1, LED1.anode
  N3: LED1.cathode, DC_Power1.V-
  N4: DC_Power1.V+, VM1.A_Probe

notes:
  5.0
  0.01
