# Fritzing sketch motorDC-driver-micro (saved by Fritzing 0.9.6b)
breadboards: 1

parts:
  DC_Power3 = DC Power Supply [part_number="6 V" package="DC Power"]
  Q1 = NPN-Transistor [part_number=2n2222a package="SOT-23 [SMD]"]
  M1 = DC Motor
  R1 = Resistor [tolerance=±5% resistance=1k package="0603 [SMD]"]
  U2 = NodeMCU V3.0

nets:
  N1: DC_Power3.V+, M1.pin_2
  N2: DC_Power3.V-, Q1.2, U2.GND
  N3: Q1.0, R1.Pin_1
  N4: Q1.1, M1.pin_1
  N5: R1.Pin_0, U2.D1
  N6: U2.D4, U2.TX, U2.CLK

notes:
  6V
  2N2222A
  Motor DC

custom parts:
  NodeMCU V3.0: NodeMcu V3 Lua WIFI Development Board
