# Fritzing sketch motorDC-driver (saved by Fritzing 0.9.6b)
breadboards: 1

parts:
  DC_Pot = DC Power Supply [part_number="1.5 V" package="DC Power"]
  DC_Motor = DC Power Supply [part_number="6 V" package="DC Power"]
  Q1 = NPN-Transistor [part_number=2n2222a package="SOT-23 [SMD]"]
  M1 = DC Motor
  R2 = Resistor [tolerance=±5% resistance=1k package="0805 [SMD]"]
  R4 = Rotary Potentiometer (Large) [maximum_resistance=100kΩ package=THT]

nets:
  N1: DC_Pot.V+, R2.Pin_0
  N2: DC_Pot.V-, DC_Motor.V-, Q1.2
  N3: DC_Motor.V+, M1.pin_2
  N4: Q1.0, R4.wiper
  N5: Q1.1, M1.pin_1
  N6: R2.Pin_1, R4.leg1

notes:
  6V
  1.5V
  2N2222A
  Potenciometro 20K
  Motor DC
  100 mA
  300 mA
