# Fritzing sketch motorDC-driver-micro-bridge-h (saved by Fritzing 0.9.6b)
breadboards: 1

parts:
  DC_Power3 = DC Power Supply [part_number="6 V" package="DC Power"]
  U1 = NodeMCU V1.0
  R1 = Resistor [tolerance=±5% resistance=1k package="2512 [SMD]"]
  R2 = Resistor [tolerance=±5% resistance=1k package="2512 [SMD]"]
  R3 = Resistor [tolerance=±5% resistance=1k package="2512 [SMD]"]
  R4 = Resistor [tolerance=±5% resistance=1k package="2512 [SMD]"]
  M1 = DC Motor
  Q1 = NPN-Transistor [package="TO92 [THT]"]
  Q2 = NPN-Transistor [package="TO92 [THT]"]
  Q3 = NPN-Transistor [package="TO92 [THT]"]
  Q4 = NPN-Transistor [package="TO92 [THT]"]

nets:
  N1: DC_Power3.V+, Q1.C, Q2.C
  N2: DC_Power3.V-, U1.GND, Q3.E, Q4.E
  N3: U1.D1, R1.Pin_1, R4.Pin_0
  N4: U1.D2, R2.Pin_0, R3.Pin_1
  N5: R1.Pin_0, Q1.B
  N6: R2.Pin_1, Q2.B
  N7: R3.Pin_0, Q3.B
  N8: R4.Pin_1, Q4.B
  N9: M1.pin_1, Q2.E, Q4.C
  N10: M1.pin_2, Q1.E, Q3.C

notes:
  6V
  2N2222A

custom parts:
  NodeMCU V1.0: ESP8266 based NodeMCU
