# Fritzing sketch motorDC-driver (saved by Fritzing 0.9.6b)
breadboards: 1

parts:
  DC_Power2 = DC Power Supply [part_number="3.3 V" package="DC Power"]
  DC_Power3 = DC Power Supply [part_number="6 V" package="DC Power"]
  Q1 = NPN-Transistor [part_number=2n2222a package="SOT-23 [SMD]"]
  R1 = Rotary Potentiometer (Large) [maximum_resistance=100kΩ package=THT]
  M1 = DC Motor

nets:
  N1: DC_Power2.V+, R1.wiper
  N2: DC_Power2.V-, DC_Power3.V-, Q1.2
  N3: DC_Power3.V+, M1.pin_2
  N4: Q1.0, R1.leg2
  N5: Q1.1, M1.pin_1

notes:
  6V
  3.3V
  2N2222A
  Potenciometro 20K
  Motor DC
